// Logisim project ep02.circ as structural Verilog: 1 circuit, main circuit main
module main (
  input  [3:0] a,
  input  [3:0] b,
  input  [3:0] in_3,
  output [3:0] out_4
);

  wire [3:0] not_1_out, not_2_out, or_1_out;

  assign not_1_out = ~a;  // NOT_Gate not_1, 4 bits wide
  assign or_1_out = a | b;  // OR_Gate or_1, 4 bits wide
  assign not_2_out = ~or_1_out;  // NOT_Gate not_2, 4 bits wide
  Multiplexer #(.select(4), .width(4), .enable("false")) multiplexer_1 (
    .in0(not_1_out), .in1(not_2_out), .in3(4'b0000), .out(out_4), .sel(in_3));  // open: in2, in4, in5, in6, in7, in8, in9, in10, in11, in12, in13, in14, in15
endmodule
